# Fritzing sketch CubeResolver (saved by Fritzing 1.0.4)
breadboards: 1

parts:
  Composant1 = Arduino Uno (Rev3)
  S2 = Pushbutton [package="[THT]"]
  S3 = Pushbutton [package="[THT]"]
  TFT1 = 1.44" SPI TFT Graphics Display 128x128 [package=THT]
  e-radionica1 = TCS230 Color Sensor [part_number=101209]

nets:
  N1: Composant1.A2, TFT1.pin7
  N2: Composant1.A3, TFT1.pin6
  N3: Composant1.D8, TFT1.pin5
  N4: Composant1.D11_PWM/MOSI, TFT1.pin4
  N5: Composant1.D13/SCK, TFT1.pin3
  N6: Composant1.D1/TX, S3.Pin_1, S3.Pin_2
  N7: Composant1.D2, S2.Pin_1, S2.Pin_2
  N8: Composant1.D3_PWM, e-radionica1.S0
  N9: Composant1.D4, e-radionica1.S1
  N10: Composant1.D5_PWM, e-radionica1.S2
  N11: Composant1.D6_PWM, e-radionica1.S3
  N12: Composant1.D7, e-radionica1.Out
  N13: Composant1.3V3, S2.Pin_3, S2.Pin_4, S3.Pin_3, S3.Pin_4, TFT1.pin2
  5V: Composant1.5V, e-radionica1.Vcc
  GND: Composant1.GND, TFT1.pin8, e-radionica1.Gnd, e-radionica1.OE

custom parts:
  1.44" SPI TFT Graphics Display 128x128: This is for https://www.amazon.com/gp/product/B07B4BDWCL/ref=ask_ql_qh_dp_hza display. Note that this display is sold with a misprinted silkscreen indicating I2C connections on P2 connector, it is actualy SPI. The P1 connections are non functional on this board from the linked URL seller on Amazon.
  TCS230 Color Sensor: TCS230
